# Fritzing sketch robot (saved by Fritzing 0.9.3b)
breadboards: 1

parts:
  Part1 = Arduino Mega 2560 (Rev3)
  hc-sr1 = hc-sr04
  U1 = 2-Channel 5v Relay Shield [package=relay-2ch5v10a]
  U2 = 2-Channel 5v Relay Shield [package=relay-2ch5v10a]
  BAT1 = 12 battery [package=battery]  # not connected
  M1 = DC Motor
  M2 = DC Motor
  Part2 = Bluetooth HC-05 Macho

nets:
  N1: Part1.D19/RX1, Part2.TXD
  N2: Part1.D18/TX1, Part2.RXD
  GND: Part1.GND, hc-sr1.GND, U1.GND, U2.GND, Part2.GND
  N3: Part1.D12_PWM, hc-sr1.Echo
  N4: Part1.D11_PWM, hc-sr1.Trig
  VCC: Part1.5V, hc-sr1.VCC, U1.VCC, U2.VCC, Part2.VCC
  N5: Part1.D4_PWM, U1.IN2
  N6: Part1.D5_PWM, U1.IN1
  N7: Part1.D6_PWM, U2.IN2
  N8: Part1.D7_PWM, U2.IN1
  N9: U1.K1-In, M1.pin_1
  N10: U1.K1-Off, U1.K2-Off
  N11: U1.K1-On, U1.K2-On
  N12: U1.K2-In, M1.pin_2
  N13: U2.K1-In, M2.pin_1
  N14: U2.K1-Off, U2.K1-On
  N15: U2.K2-In, M2.pin_2
  N16: U2.K2-Off, U2.K2-On

custom parts:
  2-Channel 5v Relay Shield: 2 Channel 5v Relay Shield w. 2x SPD-06VDC-SD-C
  12 battery: 12V lead acid type battery, like the Husqvarna YTH2448 12V 35AH battery. This is the mini version 1/4 the size of the actual battery to be closer to typical breadboard parts (around 2in wide rathher than 7in). The pads in pcb are sized to accomidate up to 14ga wire (as these batterys will deliver high currents.)
